# Fritzing sketch Termostato (saved by Fritzing 0.9.3b)
breadboards: 1

parts:
  Componente1 = Arduino Uno (Rev3)
  U1 = TMP36 [package=to-92-kit]
  LED1 = LED - 5mm [color="Green (570nm)" package="5 mm [THT]"]
  R2 = Resistor [tolerance=±5% resistance=220 package=THT]

nets:
  N1: Componente1.A0, U1.VOUT
  GND: Componente1.GND, U1.GND, R2.Pin_0
  N2: Componente1.D6_PWM, LED1.anode
  5V: Componente1.5V, U1.VCC
  N3: LED1.cathode, R2.Pin_1
